// Logisim project Dual.circ as structural Verilog: 7 circuits, main circuit Dual Core
module Dual_Core (
);

  wire clock_1_out, cmu_1_core1_read, cmu_1_core1_write, cmu_1_core2_read, cmu_1_core2_write, cmu_1_mov_en;
  wire [11:0] cmu_1_core1movadd, cmu_1_core2movadd;
  wire [15:0] cmu_1_cim_data1, cmu_1_cim_data2, cmu_1_im_add1, cmu_1_im_add2, core_1_adress_im,
       core_1_mov_out, core_2_adress_im, core_2_mov_out;
  wire [24:0] rom_1_data, rom_2_data;

  Core core_1 (
    .MV_ADDRESS(cmu_1_core1movadd), .Instruction(cmu_1_cim_data1), .DMem_Read(cmu_1_core1_read),
    .DMem_Write(cmu_1_core1_write), .CLK(clock_1_out), .Dual_Enable(cmu_1_mov_en), .MOV_IN(core_2_mov_out),
    .MOV_OUT(core_1_mov_out), .Adress_IM(core_1_adress_im));
  Core core_2 (
    .MV_ADDRESS(cmu_1_core2movadd), .Instruction(cmu_1_cim_data2), .DMem_Read(cmu_1_core2_read),
    .DMem_Write(cmu_1_core2_write), .CLK(clock_1_out), .Dual_Enable(cmu_1_mov_en), .MOV_IN(core_1_mov_out),
    .MOV_OUT(core_2_mov_out), .Adress_IM(core_2_adress_im));
  Clock clock_1 (.out(clock_1_out));
  CMU cmu_1 (
    .C_ADD1(core_1_adress_im), .CIM_DATA1(cmu_1_cim_data1), .MOV_En(cmu_1_mov_en),
    .CIM_DATA2(cmu_1_cim_data2), .C_ADD2(core_2_adress_im), .IM_ADD1(cmu_1_im_add1), .IM_DATA1(rom_1_data),
    .IM_ADD2(cmu_1_im_add2), .Core1_Read(cmu_1_core1_read), .Core1_Write(cmu_1_core1_write),
    .Core1MOVAdd(cmu_1_core1movadd), .Core2_Read(cmu_1_core2_read), .Core2_Write(cmu_1_core2_write),
    .Core2MOVAdd(cmu_1_core2movadd), .IM_DATA2(rom_2_data));
  ROM #(.addrWidth(16), .dataWidth(25)) rom_1 (.addr(cmu_1_im_add1), .data(rom_1_data), .sel(1'b1));
  ROM #(.addrWidth(16), .dataWidth(25)) rom_2 (.addr(cmu_1_im_add2), .data(rom_2_data), .sel(1'b1));
endmodule

module Core (
  input  Dual_Enable,
  input  [15:0] MOV_IN,
  input  DMem_Read,
  input  [11:0] MV_ADDRESS,
  input  DMem_Write,
  input  CLK,
  input  [15:0] Instruction,
  output [15:0] MOV_OUT,
  output [15:0] Adress_IM
);

  wire and_1_out, and_2_out, and_3_out, comparator_1_eq, comparator_1_lt, control_1_brn, control_1_brz,
       control_1_mem_ld, control_1_mem_rw, control_1_mem_sel, or_1_out, or_2_out, or_3_out, R, W;
  wire [1:0] control_1_acc_sel0;
  wire [3:0] control_1_alu_sel0;
  wire [11:0] multiplexer_3_out;
  wire [15:0] ACC, adder_1_out, alu_1_alu_out, multiplexer_1_out, multiplexer_2_out, multiplexer_4_out,
       ram_1_data, SIGNED;

  Multiplexer #(.width(16), .enable("false")) multiplexer_1 (
    .in0(16'h1), .in1({16{1'b0}}), .out(multiplexer_1_out), .sel(and_1_out));
  and and_1 (and_1_out, Dual_Enable, DMem_Write);
  Comparator #(.width(16)) comparator_1 (
    .a(ACC), .b({16{1'b0}}), .eq(comparator_1_eq), .lt(comparator_1_lt));  // open: gt
  Multiplexer #(.width(16), .enable("false")) multiplexer_2 (
    .in0(multiplexer_1_out), .in1(SIGNED), .out(multiplexer_2_out), .sel(or_1_out));
  or or_1 (or_1_out, and_3_out, and_2_out);
  and and_2 (and_2_out, control_1_brn, comparator_1_lt);
  and and_3 (and_3_out, comparator_1_eq, control_1_brz);
  Adder #(.width(16)) adder_1 (.a(Adress_IM), .b(multiplexer_2_out), .out(adder_1_out));  // open: cin, cout
  Register #(.width(16)) PC (.D(adder_1_out), .Q(Adress_IM), .clk(CLK));  // open: en, clr
  Multiplexer #(.width(12), .enable("false")) multiplexer_3 (
    .in0(Instruction[11:0]), .in1(MV_ADDRESS), .out(multiplexer_3_out), .sel(Dual_Enable));
  or or_2 (or_2_out, W, R, control_1_mem_sel);
  assign SIGNED = {{4{Instruction[11]}}, Instruction[11:0]};  // Bit_Extender bit_extender_1
  Control control_1 (
    .OP3(Instruction[15]), .OP2(Instruction[14]), .MEM_SEL(control_1_mem_sel), .OP1(Instruction[13]),
    .OP0(Instruction[12]), .MEM_LD(control_1_mem_ld), .ACC_SEL1(control_1_acc_sel0[1]),
    .ACC_SEL0(control_1_acc_sel0[0]), .MEM_RW(control_1_mem_rw), .ALU_SEL3(control_1_alu_sel0[3]),
    .ALU_SEL2(control_1_alu_sel0[2]), .ALU_SEL1(control_1_alu_sel0[1]), .ALU_SEL0(control_1_alu_sel0[0]),
    .BRZ(control_1_brz), .BRN(control_1_brn));
  RAM #(.addrWidth(12), .dataWidth(16)) ram_1 (
    .addr(multiplexer_3_out), .data(ram_1_data), .sel(or_2_out), .clk(CLK), .ld(or_3_out));  // open: clr
  or or_3 (or_3_out, control_1_mem_ld, R);
  assign ram_1_data = W ? MOV_IN : 16'bz;  // Controlled_Buffer controlled_buffer_1
  Register #(.width(16)) u_ACC (.D(multiplexer_4_out), .Q(ACC), .clk(CLK));  // open: en, clr
  Multiplexer #(.select(2), .width(16), .enable("false")) multiplexer_4 (
    .in0(ram_1_data), .in1(SIGNED), .in2(alu_1_alu_out), .out(multiplexer_4_out), .sel(control_1_acc_sel0));  // open: in3
  assign ram_1_data = control_1_mem_rw ? ACC : 16'bz;  // Controlled_Buffer controlled_buffer_2
  assign MOV_OUT = R ? ram_1_data : 16'bz;  // Controlled_Buffer controlled_buffer_3
  and and_4 (R, DMem_Read, Dual_Enable);
  and and_5 (W, Dual_Enable, DMem_Write);
  ALU alu_1 (
    .ACC(ACC), .RAM_x(ram_1_data), .x_Shift(Instruction[3:0]), .Select_ALU(control_1_alu_sel0),
    .ALU_Out(alu_1_alu_out));

  // Other names for the same wires on the sheet: SHIFT[3:0] = Instruction[3:0]

  // Notes on the sheet:
  //   OP
  //   mem_sel
  //   mem_ld
  //   RAM
  //   acc_select
  //   mem_write
  //   alu select
  //   shift_x
endmodule

module ALU (
  input  [15:0] ACC,
  input  [15:0] RAM_x,
  input  [3:0] x_Shift,
  input  [3:0] Select_ALU,
  output [15:0] ALU_Out
);

  wire [15:0] adder_1_out, and_1_out, divider_1_out, multiplier_1_out, negator_1_out, not_1_out, or_1_out,
       shifter_1_out, shifter_2_out, subtractor_1_out, xor_1_out;

  assign xor_1_out = ACC ^ RAM_x;  // XOR_Gate xor_1, 16 bits wide
  assign not_1_out = ~ACC;  // NOT_Gate not_1, 16 bits wide
  assign and_1_out = ACC & RAM_x;  // AND_Gate and_1, 16 bits wide
  assign or_1_out = ACC | RAM_x;  // OR_Gate or_1, 16 bits wide
  Adder #(.width(16)) adder_1 (.a(ACC), .b(RAM_x), .out(adder_1_out));  // open: cin, cout
  Subtractor #(.width(16)) subtractor_1 (.a(ACC), .b(RAM_x), .out(subtractor_1_out));  // open: bin, bout
  Multiplier #(.width(16)) multiplier_1 (.a(ACC), .b(RAM_x), .out(multiplier_1_out));  // open: cin, cout
  Divider #(.width(16)) divider_1 (.a(ACC), .b(RAM_x), .out(divider_1_out));  // open: upper, rem
  Negator #(.width(16)) negator_1 (.in(ACC), .out(negator_1_out));
  Shifter #(.width(16)) shifter_1 (.in(ACC), .\dist (x_Shift), .out(shifter_1_out));
  Shifter #(.width(16), .shift("lr")) shifter_2 (.in(ACC), .\dist (x_Shift), .out(shifter_2_out));
  Multiplexer #(.select(4), .width(16)) multiplexer_1 (
    .in5(xor_1_out), .in6(not_1_out), .in7(and_1_out), .in8(or_1_out), .in9(adder_1_out),
    .in10(subtractor_1_out), .in11(multiplier_1_out), .in12(divider_1_out), .in13(negator_1_out),
    .in14(shifter_1_out), .in15(shifter_2_out), .out(ALU_Out), .sel(Select_ALU));  // open: in0, in1, in2, in3, in4, en
endmodule

module Control (
  input  OP3,
  input  OP2,
  input  OP1,
  input  OP0,
  output MEM_SEL,
  output MEM_LD,
  output ACC_SEL1,
  output ACC_SEL0,
  output MEM_RW,
  output ALU_SEL3,
  output ALU_SEL2,
  output ALU_SEL1,
  output ALU_SEL0,
  output BRZ,
  output BRN
);

  wire and_1_out, and_2_out, and_3_out, and_4_out, and_5_out, and_6_out, and_7_out, and_8_out, and_9_out,
       and_10_out, and_11_out, and_12_out, not_1_out, not_2_out, not_3_out, not_4_out, not_5_out, not_6_out,
       not_7_out, not_8_out, not_9_out, not_10_out, not_11_out, not_12_out, not_13_out, not_14_out,
       not_15_out, not_16_out, not_17_out, not_18_out, not_19_out, not_20_out, not_21_out, not_22_out,
       not_23_out, not_24_out, not_25_out, not_26_out, not_27_out, not_28_out, not_29_out, not_30_out,
       not_31_out, not_32_out, not_33_out;

  not not_1 (not_1_out, OP3);
  and and_1 (and_1_out, not_1_out, OP1, OP0);
  not not_2 (not_2_out, OP3);
  and and_2 (and_2_out, not_2_out, OP2, not_3_out);
  not not_3 (not_3_out, OP1);
  and and_3 (and_3_out, OP3, not_4_out);
  not not_4 (not_4_out, OP2);
  and and_4 (and_4_out, OP3, not_5_out, not_6_out);
  not not_5 (not_5_out, OP1);
  not not_6 (not_6_out, OP0);
  not not_7 (not_7_out, OP3);
  and and_5 (and_5_out, not_7_out, OP1, OP0);
  not not_8 (not_8_out, OP3);
  and and_6 (and_6_out, not_8_out, OP2, OP0);
  and and_7 (and_7_out, OP3, not_9_out);
  not not_9 (not_9_out, OP2);
  not not_10 (not_10_out, OP1);
  and and_8 (and_8_out, OP3, not_10_out, not_11_out);
  not not_11 (not_11_out, OP0);
  not not_12 (not_12_out, OP1);
  or or_1 (ACC_SEL1, not_12_out, OP2, OP3);
  not not_13 (not_13_out, OP3);
  not not_14 (not_14_out, OP2);
  and and_9 (and_9_out, not_13_out, not_14_out, not_15_out);
  not not_15 (not_15_out, OP1);
  not not_16 (not_16_out, OP3);
  not not_17 (not_17_out, OP2);
  and and_10 (and_10_out, not_16_out, not_17_out, not_18_out);
  not not_18 (not_18_out, OP0);
  not not_19 (not_19_out, OP3);
  not not_20 (not_20_out, OP1);
  and and_11 (and_11_out, not_19_out, not_20_out, not_21_out);
  not not_21 (not_21_out, OP0);
  not not_22 (not_22_out, OP3);
  not not_23 (not_23_out, OP1);
  not not_24 (not_24_out, OP0);
  not not_25 (not_25_out, OP2);
  and and_12 (and_12_out, not_25_out, not_26_out);
  not not_26 (not_26_out, OP1);
  not not_27 (not_27_out, OP3);
  not not_28 (not_28_out, OP2);
  not not_29 (not_29_out, OP1);
  not not_30 (not_30_out, OP0);
  not not_31 (not_31_out, OP3);
  not not_32 (not_32_out, OP2);
  not not_33 (not_33_out, OP1);
  or or_2 (MEM_SEL, and_1_out, and_2_out, and_3_out, and_4_out);
  or or_3 (MEM_LD, and_5_out, and_6_out, and_7_out, and_8_out);
  or or_4 (ACC_SEL0, and_9_out, and_10_out, and_11_out);
  and and_13 (MEM_RW, not_22_out, OP2, not_23_out, not_24_out);
  or or_5 (ALU_SEL3, and_12_out, OP3);
  and and_14 (BRZ, not_27_out, not_28_out, not_29_out, not_30_out);
  and and_15 (BRN, not_31_out, not_32_out, not_33_out, OP0);

  assign ALU_SEL0 = OP0;
  assign ALU_SEL1 = OP1;
  assign ALU_SEL2 = OP2;
endmodule

module CMU (
  input  [15:0] C_ADD1,
  input  [24:0] IM_DATA1,
  input  [24:0] IM_DATA2,
  input  [15:0] C_ADD2,
  output [11:0] Core1MOVAdd,
  output Core1_Read,
  output Core1_Write,
  output [15:0] IM_ADD1,
  output [15:0] CIM_DATA1,
  output MOV_En,
  output [15:0] CIM_DATA2,
  output [15:0] IM_ADD2,
  output [11:0] Core2MOVAdd,
  output Core2_Read,
  output Core2_Write
);

  or or_1 (MOV_En, IM_DATA1[24], IM_DATA2[24]);
  not not_1 (Core1_Write, IM_DATA1[24]);
  not not_2 (Core2_Write, IM_DATA2[24]);
  Multiplexer #(.width(12), .enable("false")) multiplexer_1 (
    .in0(IM_DATA1[23:12]), .in1(IM_DATA2[11:0]), .out(Core1MOVAdd), .sel(Core1_Write));
  Multiplexer #(.width(12), .enable("false")) multiplexer_2 (
    .in0(IM_DATA2[23:12]), .in1(IM_DATA1[11:0]), .out(Core2MOVAdd), .sel(Core2_Write));

  assign CIM_DATA1 = IM_DATA1[15:0];
  assign CIM_DATA2 = IM_DATA2[15:0];
  assign Core1_Read = IM_DATA1[24];
  assign Core2_Read = IM_DATA2[24];
  assign IM_ADD1 = C_ADD1;
  assign IM_ADD2 = C_ADD2;
endmodule

module Single_Core (
);

  wire and_1_out, and_2_out, clock_1_out, comparator_1_eq, comparator_1_lt, control_1_brn, control_1_brz,
       control_1_mem_ld, control_1_mem_rw, control_1_mem_sel, or_1_out;
  wire [1:0] control_1_acc_sel0;
  wire [3:0] control_1_alu_sel0, SHIFT;
  wire [15:0] ACC, adder_1_out, alu_1_alu_out, multiplexer_1_out, multiplexer_2_out, PC_q, ram_1_data, SIGNED;
  wire [15:4] rom_1_data;

  or or_1 (or_1_out, and_1_out, and_2_out);
  and and_1 (and_1_out, comparator_1_eq, control_1_brz);
  Comparator #(.width(16)) comparator_1 (
    .a(ACC), .b({16{1'b0}}), .eq(comparator_1_eq), .lt(comparator_1_lt));  // open: gt
  Multiplexer #(.width(16), .enable("false")) multiplexer_1 (
    .in0(16'h1), .in1(SIGNED), .out(multiplexer_1_out), .sel(or_1_out));
  and and_2 (and_2_out, control_1_brn, comparator_1_lt);
  Adder #(.width(16)) adder_1 (.a(PC_q), .b(multiplexer_1_out), .out(adder_1_out));  // open: cin, cout
  Register #(.width(16)) PC (.D(adder_1_out), .Q(PC_q), .clk(clock_1_out));  // open: en, clr
  ROM #(.addrWidth(16), .dataWidth(16)) rom_1 (.addr(PC_q), .data({rom_1_data, SHIFT}), .sel(1'b1));
  Clock clock_1 (.out(clock_1_out));
  Control control_1 (
    .OP3(rom_1_data[15]), .OP2(rom_1_data[14]), .MEM_SEL(control_1_mem_sel), .OP1(rom_1_data[13]),
    .OP0(rom_1_data[12]), .MEM_LD(control_1_mem_ld), .ACC_SEL1(control_1_acc_sel0[1]),
    .ACC_SEL0(control_1_acc_sel0[0]), .MEM_RW(control_1_mem_rw), .ALU_SEL3(control_1_alu_sel0[3]),
    .ALU_SEL2(control_1_alu_sel0[2]), .ALU_SEL1(control_1_alu_sel0[1]), .ALU_SEL0(control_1_alu_sel0[0]),
    .BRZ(control_1_brz), .BRN(control_1_brn));
  assign SIGNED = {{4{rom_1_data[11]}}, {rom_1_data[11:4], SHIFT}};  // Bit_Extender bit_extender_1
  RAM #(.addrWidth(12), .dataWidth(16)) ram_1 (
    .addr({rom_1_data[11:4], SHIFT}), .data(ram_1_data), .sel(control_1_mem_sel), .clk(clock_1_out),
    .ld(control_1_mem_ld));  // open: clr
  Multiplexer #(.select(2), .width(16)) multiplexer_2 (
    .in0(ram_1_data), .in1(SIGNED), .in2(alu_1_alu_out), .out(multiplexer_2_out), .sel(control_1_acc_sel0));  // open: in3, en
  assign ram_1_data = control_1_mem_rw ? ACC : 16'bz;  // Controlled_Buffer controlled_buffer_1
  Register #(.width(16)) u_ACC (.D(multiplexer_2_out), .Q(ACC), .clk(clock_1_out));  // open: en, clr
  ALU alu_1 (.ACC(ACC), .RAM_x(ram_1_data), .x_Shift(SHIFT), .Select_ALU(control_1_alu_sel0), .ALU_Out(alu_1_alu_out));

  // Notes on the sheet:
  //   contents of rom_1 (hex, n*v repeats v):
  //   200c 4001 9001 4002 2000 2 200a 200f
  //   OP
  //   immedate address 12 bit
  //   mem_sel
  //   mem_ld
  //   acc_select
  //   MEM Write
  //   mem_write
  //   alu select
  //   shift_x
endmodule

module example (
  input  [11:0] in_1,
  input  in_2,
  input  in_3,
  input  in_4,
  input  in_5,
  input  [15:0] in_6,
  input  [15:0] in_7,
  input  [15:0] in_8,
  input  [15:0] in_9,
  input  [1:0] in_10,
  input  in_11,
  output [15:0] out_12,
  output [15:0] out_13,
  output [15:0] out_14,
  output out_15
);

  wire clock_1_out;
  wire [15:0] multiplexer_1_out;

  Multiplexer #(.select(2), .width(16), .enable("false")) multiplexer_1 (
    .in0(in_7), .in1(in_8), .in2(in_9), .out(multiplexer_1_out), .sel(in_10));  // open: in3
  RAM #(.addrWidth(12), .dataWidth(16)) ram_1 (
    .addr(in_1), .data(out_12), .sel(in_3), .clk(clock_1_out), .ld(in_4));  // open: clr
  Clock clock_1 (.out(clock_1_out));
  Register #(.width(16)) register_1 (.D(multiplexer_1_out), .clk(in_11));  // open: en, Q, clr
  assign out_12 = in_5 ? in_6 : 16'bz;  // Controlled_Buffer controlled_buffer_1
  Multiplexer #(.width(16)) multiplexer_2 (.in1(in_6), .out(out_14), .sel(in_5));  // open: in0, en
  Control control_1 ();  // open: OP3, OP2, MEM_SEL, OP1, OP0, MEM_LD, ACC_SEL1, ACC_SEL0, MEM_RW, ALU_SEL3, ALU_SEL2, ALU_SEL1, ALU_SEL0, BRZ, BRN

  assign out_13 = out_12;
  assign out_15 = in_2;

  // Other names for the same wires on the sheet: a = in_2
endmodule
